// Logisim project new_arc.circ as structural Verilog: 7 circuits, main circuit main
module main (
  input  [6:0] in_1,
  input  in_2,
  input  in_3,
  input  in_4,
  input  in_5,
  input  in_6,
  input  in_7,
  input  in_8,
  input  in_9,
  input  in_10,
  input  in_11,
  input  in_12,
  output [7:0] A,
  output [7:0] out_14,
  output [7:0] out_15,
  output [7:0] X,
  output [7:0] out_17
);

  wire clock_1_out;
  wire [7:0] n8bit_counter_1_output;

  Clock clock_1 (.out(clock_1_out));
  _8bit_reg u_8bit_reg_1 (
    .clk(clock_1_out), .select(in_2), .out_8(out_15), .out_enable(in_3), .out_7(A), .in_1(out_15),
    .in_2(out_14), ._0___data_bus(in_4));
  _8bit_reg u_8bit_reg_2 (
    .clk(clock_1_out), .select(in_5), .out_8(out_15), .out_enable(in_6), .out_7(X), .in_1(out_15),
    ._0___data_bus(1'b0));  // open: in_2
  _8bit_reg u_8bit_reg_3 (
    .clk(clock_1_out), .select(in_7), .out_8(out_15), .out_enable(in_8), .in_1(out_15), ._0___data_bus(1'b0));  // open: out_7, in_2
  ALU alu_1 (.in_1(A), .in_3(out_15), .out_5(out_15), .in_2(in_1), .out_4(out_14));
  _8bit_counter u_8bit_counter_1 (
    .count(clock_1_out), .inp_en(in_10), .in_4(out_15), .DISPLAY(out_17), .in_5(in_11),
    .OUTPUT(n8bit_counter_1_output), .in_2(in_9));
  RAM ram_1 (.addr(n8bit_counter_1_output), .data(out_15), .sel(in_12));  // open: clk, ld, clr

  // Notes on the sheet:
  //   Y
endmodule

module _8bit_reg (
  input  [7:0] in_1,
  input  [7:0] in_2,
  input  clk,
  input  select,
  input  out_enable,
  input  _0___data_bus,
  output [7:0] out_7,
  output [7:0] out_8
);

  wire and_1_out;
  wire [7:0] multiplexer_1_out;

  and and_1 (and_1_out, clk, select);
  Multiplexer #(.width(8), .enable("false")) multiplexer_1 (
    .in0(in_1), .in1(in_2), .out(multiplexer_1_out), .sel(_0___data_bus));
  D_Flip_Flop #(.trigger("falling")) d_ff_1 (
    .clk(and_1_out), .D(multiplexer_1_out[0]), .Q(out_7[0]));  // open: Qn, preset, en, reset
  D_Flip_Flop #(.trigger("falling")) d_ff_2 (
    .clk(and_1_out), .D(multiplexer_1_out[1]), .Q(out_7[1]));  // open: Qn, preset, en, reset
  D_Flip_Flop #(.trigger("falling")) d_ff_3 (
    .clk(and_1_out), .D(multiplexer_1_out[2]), .Q(out_7[2]));  // open: Qn, preset, en, reset
  D_Flip_Flop #(.trigger("falling")) d_ff_4 (
    .clk(and_1_out), .D(multiplexer_1_out[3]), .Q(out_7[3]));  // open: Qn, preset, en, reset
  D_Flip_Flop #(.trigger("falling")) d_ff_5 (
    .clk(and_1_out), .D(multiplexer_1_out[4]), .Q(out_7[4]));  // open: Qn, preset, en, reset
  D_Flip_Flop #(.trigger("falling")) d_ff_6 (
    .clk(and_1_out), .D(multiplexer_1_out[5]), .Q(out_7[5]));  // open: Qn, preset, en, reset
  D_Flip_Flop #(.trigger("falling")) d_ff_7 (
    .clk(and_1_out), .D(multiplexer_1_out[6]), .Q(out_7[6]));  // open: Qn, preset, en, reset
  D_Flip_Flop #(.trigger("falling")) d_ff_8 (
    .clk(and_1_out), .D(multiplexer_1_out[7]), .Q(out_7[7]));  // open: Qn, preset, en, reset
  assign out_8 = out_enable ? out_7 : 8'bz;  // Controlled_Buffer controlled_buffer_1

  // Notes on the sheet:
  //   data bus
  //   alu
  //   1 -> ALU
endmodule

module ALU (
  input  [7:0] in_1,
  input  [6:0] in_2,
  input  [7:0] in_3,
  output [7:0] out_4,
  output [7:0] out_5
);

  wire [7:0] adder_1_out, and_1_out, controled_inv_1_out_3, controled_inv_2_out_3, multiplexer_1_out,
       multiplexer_2_out, multiplexer_3_out;

  Multiplexer #(.width(8), .enable("false")) multiplexer_1 (
    .in0(in_1), .in1({8{1'b0}}), .out(multiplexer_1_out), .sel(in_2[0]));
  controled_inv controled_inv_1 (.in_1(multiplexer_1_out), .in_2(in_2[1]), .out_3(controled_inv_1_out_3));
  Multiplexer #(.width(8), .enable("false")) multiplexer_2 (
    .in0(in_3), .in1({8{1'b0}}), .out(multiplexer_2_out), .sel(in_2[2]));
  controled_inv controled_inv_2 (.in_1(multiplexer_2_out), .in_2(in_2[3]), .out_3(controled_inv_2_out_3));
  Adder adder_1 (.a(controled_inv_1_out_3), .b(controled_inv_2_out_3), .out(adder_1_out));  // open: cin, cout
  assign and_1_out = controled_inv_1_out_3 & controled_inv_2_out_3;  // AND_Gate and_1, 8 bits wide
  Multiplexer #(.width(8), .enable("false")) multiplexer_3 (
    .in0(adder_1_out), .in1(and_1_out), .out(multiplexer_3_out), .sel(in_2[5]));
  controled_inv controled_inv_3 (.in_1(multiplexer_3_out), .in_2(in_2[4]), .out_3(out_4));
  assign out_5 = in_2[6] ? out_4 : 8'bz;  // Controlled_Buffer controlled_buffer_1

  // Notes on the sheet:
  //   X
  //   Z x
  //   INV X
  //   Y
  //   Z y
  //   INV Y
  //   INV out
  //   X+Y||X&Y
  //   0           1
endmodule

module controled_inv (
  input  [7:0] in_1,
  input  in_2,
  output [7:0] out_3
);

  xor xor_1 (out_3[0], in_1[0], in_2);
  xor xor_2 (out_3[1], in_1[1], in_2);
  xor xor_3 (out_3[2], in_1[2], in_2);
  xor xor_4 (out_3[3], in_1[3], in_2);
  xor xor_5 (out_3[4], in_1[4], in_2);
  xor xor_6 (out_3[5], in_1[5], in_2);
  xor xor_7 (out_3[6], in_1[6], in_2);
  xor xor_8 (out_3[7], in_1[7], in_2);
endmodule

module _8bit_counter (
  input  count,
  input  in_2,
  input  inp_en,
  input  [7:0] in_4,
  input  in_5,
  output [7:0] DISPLAY,
  output [7:0] OUTPUT
);

  wire and_1_out, and_2_out, d_ff_1_qn, d_ff_2_qn, d_ff_3_qn, d_ff_4_qn, d_ff_5_qn, d_ff_6_qn, d_ff_7_qn,
       d_ff_8_qn, multiplexer_1_out, multiplexer_2_out, multiplexer_3_out, multiplexer_4_out,
       multiplexer_5_out, multiplexer_6_out, multiplexer_7_out, multiplexer_8_out, multiplexer_9_out,
       multiplexer_10_out, multiplexer_11_out, multiplexer_12_out, multiplexer_13_out, multiplexer_14_out,
       multiplexer_15_out, multiplexer_16_out;

  and and_1 (and_1_out, count, in_2);
  and and_2 (and_2_out, in_2, inp_en);
  Multiplexer #(.enable("false")) multiplexer_1 (
    .in0(and_1_out), .in1(and_1_out), .out(multiplexer_1_out), .sel(and_2_out));
  Multiplexer #(.enable("false")) multiplexer_2 (
    .in0(d_ff_1_qn), .in1(in_4[0]), .out(multiplexer_2_out), .sel(and_2_out));
  Multiplexer #(.enable("false")) multiplexer_3 (
    .in0(DISPLAY[0]), .in1(and_1_out), .out(multiplexer_3_out), .sel(and_2_out));
  Multiplexer #(.enable("false")) multiplexer_4 (
    .in0(d_ff_2_qn), .in1(in_4[1]), .out(multiplexer_4_out), .sel(and_2_out));
  Multiplexer #(.enable("false")) multiplexer_5 (
    .in0(DISPLAY[1]), .in1(and_1_out), .out(multiplexer_5_out), .sel(and_2_out));
  Multiplexer #(.enable("false")) multiplexer_6 (
    .in0(d_ff_3_qn), .in1(in_4[2]), .out(multiplexer_6_out), .sel(and_2_out));
  Multiplexer #(.enable("false")) multiplexer_7 (
    .in0(DISPLAY[2]), .in1(and_1_out), .out(multiplexer_7_out), .sel(and_2_out));
  Multiplexer #(.enable("false")) multiplexer_8 (
    .in0(d_ff_4_qn), .in1(in_4[3]), .out(multiplexer_8_out), .sel(and_2_out));
  Multiplexer #(.enable("false")) multiplexer_9 (
    .in0(DISPLAY[3]), .in1(and_1_out), .out(multiplexer_9_out), .sel(and_2_out));
  Multiplexer #(.enable("false")) multiplexer_10 (
    .in0(d_ff_5_qn), .in1(in_4[4]), .out(multiplexer_10_out), .sel(and_2_out));
  Multiplexer #(.enable("false")) multiplexer_11 (
    .in0(DISPLAY[4]), .in1(and_1_out), .out(multiplexer_11_out), .sel(and_2_out));
  Multiplexer #(.enable("false")) multiplexer_12 (
    .in0(d_ff_6_qn), .in1(in_4[5]), .out(multiplexer_12_out), .sel(and_2_out));
  Multiplexer #(.enable("false")) multiplexer_13 (
    .in0(DISPLAY[5]), .in1(and_1_out), .out(multiplexer_13_out), .sel(and_2_out));
  Multiplexer #(.enable("false")) multiplexer_14 (
    .in0(d_ff_7_qn), .in1(in_4[6]), .out(multiplexer_14_out), .sel(and_2_out));
  Multiplexer #(.enable("false")) multiplexer_15 (
    .in0(DISPLAY[6]), .in1(and_1_out), .out(multiplexer_15_out), .sel(and_2_out));
  Multiplexer #(.enable("false")) multiplexer_16 (
    .in0(d_ff_8_qn), .in1(in_4[7]), .out(multiplexer_16_out), .sel(and_2_out));
  D_Flip_Flop #(.trigger("falling")) d_ff_1 (
    .clk(multiplexer_1_out), .D(multiplexer_2_out), .Q(DISPLAY[0]), .Qn(d_ff_1_qn));  // open: preset, en, reset
  D_Flip_Flop #(.trigger("falling")) d_ff_2 (
    .clk(multiplexer_3_out), .D(multiplexer_4_out), .Q(DISPLAY[1]), .Qn(d_ff_2_qn));  // open: preset, en, reset
  D_Flip_Flop #(.trigger("falling")) d_ff_3 (
    .clk(multiplexer_5_out), .D(multiplexer_6_out), .Q(DISPLAY[2]), .Qn(d_ff_3_qn));  // open: preset, en, reset
  D_Flip_Flop #(.trigger("falling")) d_ff_4 (
    .clk(multiplexer_7_out), .D(multiplexer_8_out), .Q(DISPLAY[3]), .Qn(d_ff_4_qn));  // open: preset, en, reset
  D_Flip_Flop #(.trigger("falling")) d_ff_5 (
    .clk(multiplexer_9_out), .D(multiplexer_10_out), .Q(DISPLAY[4]), .Qn(d_ff_5_qn));  // open: preset, en, reset
  D_Flip_Flop #(.trigger("falling")) d_ff_6 (
    .clk(multiplexer_11_out), .D(multiplexer_12_out), .Q(DISPLAY[5]), .Qn(d_ff_6_qn));  // open: preset, en, reset
  D_Flip_Flop #(.trigger("falling")) d_ff_7 (
    .clk(multiplexer_13_out), .D(multiplexer_14_out), .Q(DISPLAY[6]), .Qn(d_ff_7_qn));  // open: preset, en, reset
  D_Flip_Flop #(.trigger("falling")) d_ff_8 (
    .clk(multiplexer_15_out), .D(multiplexer_16_out), .Q(DISPLAY[7]), .Qn(d_ff_8_qn));  // open: preset, en, reset
  assign OUTPUT = in_5 ? DISPLAY : 8'bz;  // Controlled_Buffer controlled_buffer_1
endmodule

module _2bit_counter (
  input  in_1,
  input  in_2,
  output out_3,
  output out_4
);

  wire d_ff_1_q, d_ff_2_qn, d_ff_3_qn, not_1_out;

  D_Flip_Flop #(.trigger("falling")) d_ff_1 (
    .clk(in_1), .D(in_2), .Q(d_ff_1_q), .reset(not_1_out));  // open: Qn, preset, en
  not not_1 (not_1_out, in_2);
  D_Flip_Flop #(.trigger("falling")) d_ff_2 (
    .clk(in_1), .D(d_ff_2_qn), .Q(out_3), .Qn(d_ff_2_qn), .reset(d_ff_1_q));  // open: preset, en
  D_Flip_Flop #(.trigger("falling")) d_ff_3 (
    .clk(out_3), .D(d_ff_3_qn), .Q(out_4), .Qn(d_ff_3_qn), .reset(d_ff_1_q));  // open: preset, en
endmodule

module instruction_reg (
  input  [7:0] in_1
);

  wire nand_1_out;
  wire [4:3] n2bit_counter_1_out_3;

  _2bit_counter u_2bit_counter_1 (
    .out_3(n2bit_counter_1_out_3[3]), .out_4(n2bit_counter_1_out_3[4]));  // open: in_1, in_2
  nand nand_1 (nand_1_out, n2bit_counter_1_out_3[3], n2bit_counter_1_out_3[4]);
  _8bit_reg u_8bit_reg_1 (
    .clk(nand_1_out), .select(nand_1_out), .in_1(in_1));  // open: out_8, out_enable, out_7, in_2, _0___data_bus
  Multiplexer #(.select(5), .width(20), .enable("false")) multiplexer_1 (.sel({n2bit_counter_1_out_3, in_1[2:0]}));  // open: in0, in1, in2, in3, in4, in5, in6, in7, in8, in9, in10, in11, in12, in13, in14, in15, in16, in17, in18, in19, in20, in21, in22, in23, in24, in25, in26, in27, in28, in29, in30, in31, out

  // Notes on the sheet:
  //   ALU controll
  //   control bus
endmodule
